# Fritzing sketch water-level (saved by Fritzing 0.9.3b)
breadboards: 1

parts:
  U1 = NodeMCU V3.0
  HC-SR04_Sensor_1 = HC-SR04 Ultrasonic Distance Sensor
  R1 = Resistor [tolerance=±5% resistance=220 package=THT]

nets:
  GND: U1.GND, HC-SR04_Sensor_1.GND
  N1: U1.D5, HC-SR04_Sensor_1.TRIG
  N2: U1.D6, R1.Pin_0
  VIN: U1.Vin, HC-SR04_Sensor_1.VCC
  N3: HC-SR04_Sensor_1.ECHO, R1.Pin_1

notes:
  zf200626.1849

custom parts:
  NodeMCU V3.0: ESP8266 based NodeMCU
  HC-SR04 Ultrasonic Distance Sensor: The HC-SR04 is an ultrasonic distance sensor. It is capable of providing measurement for ranges of 2cm to 400cm. The module operates at 5V.
