# Fritzing sketch nodemcu_adc_ ADS1115 (saved by Fritzing 0.9.3b)
breadboards: 1

parts:
  U1 = NodeMCU V3.0
  Part1 = Adafruit ADS1115 16Bit I2C ADC [part_number="Adafruit #1085"]

nets:
  3V3: U1.3V3, Part1.VDD
  N1: U1.GND#6, U1.GND#13, U1.GND#16, U1.GND#33, Part1.GND
  N2: U1.D5, Part1.SDA
  N3: U1.D6, Part1.SCL

custom parts:
  NodeMCU V3.0: ESP8266 based NodeMCU
  Adafruit ADS1115 16Bit I2C ADC: For microcontrollers without an analog-to-digital converter or when you want a higher-precision ADC, the ADS1115 provides 16-bit precision at 860 samples/second over I2C. The chip can be configured as 4 single-ended input channels, or two differential channels. As a nice bonus, it even includes a programmable gain amplifier, up to x16, to help boost up smaller single/differential signals to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
