# Fritzing sketch transfo_courant_clip (saved by Fritzing 0.9.3b)
breadboards: 1

parts:
  U1 = NodeMCU V3.0
  R1 = Resistor [tolerance=±5% resistance=150 package=THT]
  R2 = Resistor [tolerance=±5% resistance=820 package=THT]
  R3 = Resistor [tolerance=±5% resistance=100 package=THT]
  J1 = Screw terminal - 2 pins [package=THT]

nets:
  N1: U1.A0, R3.Pin_1, J1.pin2
  N2: R1.Pin_1, R2.Pin_0, R3.Pin_0, J1.pin1
  3.3V: R2.Pin_1

notes:
  zf190922.2257
  transfo clip

custom parts:
  NodeMCU V3.0: ESP8266 based NodeMCU
