# Fritzing sketch nodemcu_energy_adc_ ADS1015 (saved by Fritzing 0.9.3b)
breadboards: 1

parts:
  U1 = NodeMCU V3.0
  Composant1 = Humidity Temperature Sensor SHT15

nets:
  3V3: U1.3V3, Composant1.VCC
  GND: U1.GND, Composant1.GND
  N1: U1.D5, Composant1.SDA
  N2: U1.D6, Composant1.SCL

custom parts:
  NodeMCU V3.0: ESP8266 based NodeMCU
