# Fritzing sketch transfo_courant_clip (saved by Fritzing 0.9.3b)
breadboards: 1

parts:
  U1 = NodeMCU V3.0  # not connected
  R3 = Resistor [tolerance=±5% resistance=100 package=THT]
  HC-SR04_Sensor_1 = HC-SR04 Ultrasonic Distance Sensor

nets:
  N1: R3.Pin_1, HC-SR04_Sensor_1.GND

notes:
  zf200625.2032
  transfo clip

custom parts:
  NodeMCU V3.0: ESP8266 based NodeMCU
