# Fritzing sketch play_file (saved by Fritzing 0.9.3b)
breadboards: 1

parts:
  U1 = NodeMCU V3.0
  Composant1 = Adafruit PAM8302 [part_number="Adafruit #2130"]
  VCC1 = 4 x AAA Battery Mount
  SP1 = SPEAKER [package=pcb_mount_speaker]
  D1 = Diode [package=diode-1n4148]
  S1 = Pushbutton [package="[SMD]"]

nets:
  N1: U1.D3, S1.Pin_1, S1.Pin_2
  N2: U1.GND, S1.Pin_3, S1.Pin_4
  N3: U1.D5, Composant1.AIN+
  N4: U1.D6, Composant1.SD
  GND: Composant1.GND, Composant1.AIN-, VCC1.-
  5V: Composant1.VCC, D1.C
  N5: Composant1.VO+, SP1.+
  N6: Composant1.VO-, SP1.-
  N7: VCC1.+, D1.A

notes:
  zf190212.1530

custom parts:
  NodeMCU V3.0: ESP8266 based NodeMCU
  Adafruit PAM8302: This super small mono amplifier is surprisingly powerful - able to deliver up to 2.5 Watts into 4-8 ohm impedance speakers. Inside the miniature chip is a class D controller, able to run from 2.0V-5.5VDC. Since the amp is a class D, its very efficient (over 90% efficient when driving an 8Ω speaker at over half a Watt) - making it perfect for portable and battery-powered projects. It has built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
