# Fritzing sketch play_file (saved by Fritzing 0.9.3b)

parts:
  PROTO1 = PermaProto_Mint_Tin_Size_Breadboard  # not connected
  U1 = NodeMCU V3.0
  Composant1 = Adafruit PAM8302 [part_number="Adafruit #2130"]  # not connected
  VCC1 = 4 x AAA Battery Mount  # not connected
  SP1 = SPEAKER [package=pcb_mount_speaker]  # not connected

nets:
  N1: U1.GND#6, U1.GND#13, U1.GND#16, U1.GND#33

notes:
  Ce n'est pas encore terminé
  zf190210.1252

custom parts:
  NodeMCU V3.0: ESP8266 based NodeMCU
  Adafruit PAM8302: This super small mono amplifier is surprisingly powerful - able to deliver up to 2.5 Watts into 4-8 ohm impedance speakers. Inside the miniature chip is a class D controller, able to run from 2.0V-5.5VDC. Since the amp is a class D, its very efficient (over 90% efficient when driving an 8Ω speaker at over half a Watt) - making it perfect for portable and battery-powered projects. It has built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
